// Logisim project CPU.circ as structural Verilog
module Bin_Adder_1 (
  input  in_1,
  input  in_2,
  input  in_3,
  output out_4,
  output out_5
);

  wire and_1_out, and_2_out, and_3_out;

  and and_1 (and_1_out, in_1, in_3);
  and and_2 (and_2_out, in_1, in_2);
  and and_3 (and_3_out, in_2, in_3);
  or or_1 (out_4, and_1_out, and_2_out, and_3_out);
  xor xor_1 (out_5, in_1, in_2, in_3);
endmodule

module ALU (
  input  [7:0] in_1,
  input  [7:0] in_2,
  input  [3:0] in_3,
  output out_4,
  output [7:0] out_5
);

  wire adder_1_cout, decoder_1_out2, left_shift_8_1_out_2, multiplier_8_1_out_3, right_shift_8_1_out_2;
  wire [7:0] adder_1_out, and_1_out, division_8_1_out_3, division_8_1_out_4, left_shift_8_1_out_3,
       multiplexer_1_out, multiplier_8_1_out_4, not_1_out, not_2_out, or_1_out, right_shift_8_1_out_3;

  Decoder #(.select(4), .enable("false")) decoder_1 (
    .out2(decoder_1_out2), .sel(in_3));  // open: out0, out1, out3, out4, out5, out6, out7, out8, out9, out10, out11, out12, out13, out14, out15
  assign not_1_out = ~in_2;  // NOT_Gate not_1, 8 bits wide
  Multiplexer #(.select(4), .width(8), .enable("false")) multiplexer_1 (
    .in0(in_2), .in1(in_2), .in2(not_1_out), .in3({8{1'b0}}), .in4({8{1'b0}}), .in5({8{1'b0}}),
    .in6({8{1'b0}}), .in7({8{1'b0}}), .in8({8{1'b0}}), .in9(in_2), .in10({8{1'b0}}), .in11(in_2),
    .in12(in_2), .in13({8{1'b0}}), .in14({8{1'b0}}), .in15({8{1'b0}}), .out(multiplexer_1_out), .sel(in_3));
  Adder adder_1 (.a(in_1), .b(multiplexer_1_out), .out(adder_1_out), .cin(decoder_1_out2), .cout(adder_1_cout));
  assign and_1_out = in_1 & in_2;  // AND_Gate and_1, 8 bits wide
  assign or_1_out = in_1 | in_2;  // OR_Gate or_1, 8 bits wide
  assign not_2_out = ~in_1;  // NOT_Gate not_2, 8 bits wide
  left_shift_8 left_shift_8_1 (.in_1(in_1), .out_3(left_shift_8_1_out_3), .out_2(left_shift_8_1_out_2));
  Multiplier_8 multiplier_8_1 (
    .in_1(in_1), .in_2(multiplexer_1_out), .out_3(multiplier_8_1_out_3), .out_4(multiplier_8_1_out_4));
  right_shift_8 right_shift_8_1 (.in_1(in_1), .out_3(right_shift_8_1_out_3), .out_2(right_shift_8_1_out_2));
  Division_8 division_8_1 (
    .in_1(in_1), .in_2(multiplexer_1_out), .out_3(division_8_1_out_3), .out_4(division_8_1_out_4));
  Multiplexer #(.select(4), .enable("false")) multiplexer_2 (
    .in0(1'b0), .in1(adder_1_cout), .in2(adder_1_cout), .in3(adder_1_cout), .in4(1'b0), .in5(1'b0),
    .in6(1'b0), .in7(left_shift_8_1_out_2), .in8(right_shift_8_1_out_2), .in9(multiplier_8_1_out_3),
    .in10(multiplier_8_1_out_3), .in11(1'b0), .in12(1'b0), .in13(1'b0), .in14(1'b0), .in15(1'b0),
    .out(out_4), .sel(in_3));
  Multiplexer #(.select(4), .width(8), .enable("false")) multiplexer_3 (
    .in0({8{1'b0}}), .in1(adder_1_out), .in2(adder_1_out), .in3(adder_1_out), .in4(and_1_out),
    .in5(or_1_out), .in6(not_2_out), .in7(left_shift_8_1_out_3), .in8(right_shift_8_1_out_3),
    .in9(multiplier_8_1_out_4), .in10(multiplier_8_1_out_4), .in11(division_8_1_out_3),
    .in12(division_8_1_out_4), .in13(division_8_1_out_3), .out(out_5), .sel(in_3));  // open: in14, in15

  // Notes on the sheet:
  //   0001 - add
  //   0010 - sub
  //   0011 - thru
  //   0100 - and
  //   0101 - or
  //   0110 - not
  //   1000 right shift
  //   1001 - mult
  //   1010 - set to 0
  //   1011 - div
  //   1100 - mod
  //   1101 - set to 1
  //   0111 - left shift
endmodule

module Binary_Adder_8 (
  input  [7:0] in_1,
  input  [7:0] in_2,
  input  in_3,
  output out_4,
  output [7:0] out_5
);

  wire bin_adder_1_2_out_4, bin_adder_1_3_out_4, bin_adder_1_4_out_4, bin_adder_1_5_out_4,
       bin_adder_1_6_out_4, bin_adder_1_7_out_4, bin_adder_1_8_out_4;

  Bin_Adder_1 bin_adder_1_1 (
    .in_1(in_1[7]), .in_2(in_2[7]), .in_3(bin_adder_1_2_out_4), .out_4(out_4), .out_5(out_5[7]));
  Bin_Adder_1 bin_adder_1_2 (
    .in_1(in_1[6]), .in_2(in_2[6]), .in_3(bin_adder_1_3_out_4), .out_4(bin_adder_1_2_out_4), .out_5(out_5[6]));
  Bin_Adder_1 bin_adder_1_3 (
    .in_1(in_1[5]), .in_2(in_2[5]), .in_3(bin_adder_1_4_out_4), .out_4(bin_adder_1_3_out_4), .out_5(out_5[5]));
  Bin_Adder_1 bin_adder_1_4 (
    .in_1(in_1[4]), .in_2(in_2[4]), .in_3(bin_adder_1_5_out_4), .out_4(bin_adder_1_4_out_4), .out_5(out_5[4]));
  Bin_Adder_1 bin_adder_1_5 (
    .in_1(in_1[3]), .in_2(in_2[3]), .in_3(bin_adder_1_6_out_4), .out_4(bin_adder_1_5_out_4), .out_5(out_5[3]));
  Bin_Adder_1 bin_adder_1_6 (
    .in_1(in_1[2]), .in_2(in_2[2]), .in_3(bin_adder_1_7_out_4), .out_4(bin_adder_1_6_out_4), .out_5(out_5[2]));
  Bin_Adder_1 bin_adder_1_7 (
    .in_1(in_1[1]), .in_2(in_2[1]), .in_3(bin_adder_1_8_out_4), .out_4(bin_adder_1_7_out_4), .out_5(out_5[1]));
  Bin_Adder_1 bin_adder_1_8 (
    .in_1(in_1[0]), .in_2(in_2[0]), .in_3(in_3), .out_4(bin_adder_1_8_out_4), .out_5(out_5[0]));
endmodule

module flipper_8 (
  input  [7:0] in_1,
  output [7:0] out_2
);

  not not_1 (out_2[0], in_1[0]);
  not not_2 (out_2[1], in_1[1]);
  not not_3 (out_2[2], in_1[2]);
  not not_4 (out_2[3], in_1[3]);
  not not_5 (out_2[4], in_1[4]);
  not not_6 (out_2[5], in_1[5]);
  not not_7 (out_2[6], in_1[6]);
  not not_8 (out_2[7], in_1[7]);
endmodule

module left_shift_8 (
  input  [7:0] in_1,
  output out_2,
  output [7:0] out_3
);


  assign out_2 = in_1[7];
  assign out_3 = {in_1[6:0], 1'b0};
endmodule

module right_shift_8 (
  input  [7:0] in_1,
  output out_2,
  output [7:0] out_3
);


  assign out_2 = in_1[0];
  assign out_3 = {1'b0, in_1[7:1]};
endmodule

module Decoder_2 (
  input  in_1,
  input  in_2,
  output out_3,
  output out_4,
  output out_5,
  output out_6
);

  wire not_1_out, not_2_out;

  not not_1 (not_1_out, in_1);
  not not_2 (not_2_out, in_2);
  and and_1 (out_3, in_1, in_2, 1'b1);
  and and_2 (out_4, in_1, not_2_out, 1'b1);
  and and_3 (out_5, not_1_out, in_2, 1'b1);
  and and_4 (out_6, not_1_out, not_2_out, 1'b1);
endmodule

module Register_1 (
  input  in_1,
  input  in_2,
  output out_3
);

  wire nand_1_out, nand_2_out, nand_3_out, nand_5_out;

  nand nand_1 (nand_1_out, in_1, in_1);
  nand nand_2 (nand_2_out, in_1, in_2);
  nand nand_3 (nand_3_out, in_2, nand_1_out);
  nand nand_4 (out_3, nand_2_out, nand_5_out);
  nand nand_5 (nand_5_out, out_3, nand_3_out);
endmodule

module Register_8 (
  input  in_1,
  input  [7:0] in_2,
  input  in_3,
  output [7:0] out_4
);

  Register_1 register_1_1 (.in_2(in_3), .out_3(out_4[7]), .in_1(in_2[7]));
  Register_1 register_1_2 (.in_2(in_3), .out_3(out_4[6]), .in_1(in_2[6]));
  Register_1 register_1_3 (.in_2(in_3), .out_3(out_4[5]), .in_1(in_2[5]));
  Register_1 register_1_4 (.in_2(in_3), .out_3(out_4[4]), .in_1(in_2[4]));
  Register_1 register_1_5 (.in_2(in_3), .out_3(out_4[6]), .in_1(in_2[3]));
  Register_1 register_1_6 (.in_2(in_3), .out_3(out_4[5]), .in_1(in_2[2]));
  Register_1 register_1_7 (.in_2(in_3), .out_3(out_4[1]), .in_1(in_2[1]));
  Register_1 register_1_8 (.in_2(in_3), .out_3(out_4[0]), .in_1(in_2[0]));

  assign out_4[3:2] = out_4[6:5];
endmodule

module Multiplier_8 (
  input  [7:0] in_1,
  input  [7:0] in_2,
  output out_3,
  output [7:0] out_4
);

  wire adder_1_cout, adder_2_cout, adder_3_cout, adder_4_cout, adder_5_cout, adder_6_cout, adder_7_cout,
       left_shift_8_28_out_2, or_2_out;
  wire [1:0] left_shift_8_27_out_2;
  wire [2:0] left_shift_8_25_out_2;
  wire [3:0] left_shift_8_22_out_2;
  wire [4:0] left_shift_8_18_out_2;
  wire [5:0] left_shift_8_12_out_2;
  wire [6:0] left_shift_8_6_out_2;
  wire [7:0] adder_1_out, adder_2_out, adder_3_out, adder_4_out, adder_5_out, adder_6_out,
       left_shift_8_1_out_3, left_shift_8_2_out_3, left_shift_8_3_out_3, left_shift_8_4_out_3,
       left_shift_8_5_out_3, left_shift_8_6_out_3, left_shift_8_7_out_3, left_shift_8_8_out_3,
       left_shift_8_9_out_3, left_shift_8_10_out_3, left_shift_8_11_out_3, left_shift_8_12_out_3,
       left_shift_8_13_out_3, left_shift_8_14_out_3, left_shift_8_15_out_3, left_shift_8_16_out_3,
       left_shift_8_17_out_3, left_shift_8_18_out_3, left_shift_8_19_out_3, left_shift_8_20_out_3,
       left_shift_8_21_out_3, left_shift_8_22_out_3, left_shift_8_23_out_3, left_shift_8_24_out_3,
       left_shift_8_25_out_3, left_shift_8_26_out_3, left_shift_8_27_out_3, left_shift_8_28_out_3,
       one_on_eight_1_out_3, one_on_eight_2_out_3, one_on_eight_3_out_3, one_on_eight_4_out_3,
       one_on_eight_5_out_3, one_on_eight_6_out_3, one_on_eight_7_out_3, one_on_eight_8_out_3;

  one_on_eight one_on_eight_1 (.in_1(in_1), .in_2(in_2[7]), .out_3(one_on_eight_1_out_3));
  one_on_eight one_on_eight_2 (.in_1(in_1), .in_2(in_2[6]), .out_3(one_on_eight_2_out_3));
  one_on_eight one_on_eight_3 (.in_1(in_1), .in_2(in_2[5]), .out_3(one_on_eight_3_out_3));
  one_on_eight one_on_eight_4 (.in_1(in_1), .in_2(in_2[4]), .out_3(one_on_eight_4_out_3));
  one_on_eight one_on_eight_5 (.in_1(in_1), .in_2(in_2[3]), .out_3(one_on_eight_5_out_3));
  one_on_eight one_on_eight_6 (.in_1(in_1), .in_2(in_2[2]), .out_3(one_on_eight_6_out_3));
  one_on_eight one_on_eight_7 (.in_1(in_1), .in_2(in_2[1]), .out_3(one_on_eight_7_out_3));
  one_on_eight one_on_eight_8 (.in_1(in_1), .in_2(in_2[0]), .out_3(one_on_eight_8_out_3));
  left_shift_8 left_shift_8_1 (
    .in_1(one_on_eight_1_out_3), .out_3(left_shift_8_1_out_3), .out_2(left_shift_8_6_out_2[6]));
  left_shift_8 left_shift_8_2 (
    .in_1(left_shift_8_1_out_3), .out_3(left_shift_8_2_out_3), .out_2(left_shift_8_6_out_2[5]));
  left_shift_8 left_shift_8_3 (
    .in_1(left_shift_8_2_out_3), .out_3(left_shift_8_3_out_3), .out_2(left_shift_8_6_out_2[4]));
  or or_1 (out_3, left_shift_8_6_out_2[6], left_shift_8_6_out_2[5], left_shift_8_6_out_2[4], left_shift_8_6_out_2[3], left_shift_8_6_out_2[2], left_shift_8_6_out_2[1], left_shift_8_6_out_2[0], left_shift_8_12_out_2[5], left_shift_8_12_out_2[4], left_shift_8_12_out_2[3], left_shift_8_12_out_2[2], left_shift_8_12_out_2[1], left_shift_8_12_out_2[0], left_shift_8_18_out_2[4], left_shift_8_18_out_2[3], left_shift_8_18_out_2[2], left_shift_8_18_out_2[1], left_shift_8_18_out_2[0], left_shift_8_22_out_2[3], left_shift_8_22_out_2[2], left_shift_8_22_out_2[1], left_shift_8_22_out_2[0], left_shift_8_25_out_2[2], left_shift_8_25_out_2[1], left_shift_8_25_out_2[0], left_shift_8_27_out_2[1], left_shift_8_27_out_2[0], or_2_out);
  left_shift_8 left_shift_8_4 (
    .in_1(left_shift_8_3_out_3), .out_3(left_shift_8_4_out_3), .out_2(left_shift_8_6_out_2[3]));
  left_shift_8 left_shift_8_5 (
    .in_1(left_shift_8_4_out_3), .out_3(left_shift_8_5_out_3), .out_2(left_shift_8_6_out_2[2]));
  Adder adder_1 (
    .a(one_on_eight_8_out_3), .b(left_shift_8_6_out_3), .out(adder_1_out), .cin(1'b0), .cout(adder_1_cout));
  left_shift_8 left_shift_8_6 (
    .in_1(left_shift_8_7_out_3), .out_3(left_shift_8_6_out_3), .out_2(left_shift_8_6_out_2[0]));
  left_shift_8 left_shift_8_7 (
    .in_1(left_shift_8_5_out_3), .out_3(left_shift_8_7_out_3), .out_2(left_shift_8_6_out_2[1]));
  Adder adder_2 (
    .a(adder_1_out), .b(left_shift_8_12_out_3), .out(adder_2_out), .cin(adder_1_cout), .cout(adder_2_cout));
  left_shift_8 left_shift_8_8 (
    .in_1(left_shift_8_9_out_3), .out_3(left_shift_8_8_out_3), .out_2(left_shift_8_12_out_2[4]));
  left_shift_8 left_shift_8_9 (
    .in_1(one_on_eight_2_out_3), .out_3(left_shift_8_9_out_3), .out_2(left_shift_8_12_out_2[5]));
  Adder adder_3 (
    .a(adder_2_out), .b(left_shift_8_18_out_3), .out(adder_3_out), .cin(adder_2_cout), .cout(adder_3_cout));
  left_shift_8 left_shift_8_10 (
    .in_1(left_shift_8_8_out_3), .out_3(left_shift_8_10_out_3), .out_2(left_shift_8_12_out_2[3]));
  left_shift_8 left_shift_8_11 (
    .in_1(left_shift_8_10_out_3), .out_3(left_shift_8_11_out_3), .out_2(left_shift_8_12_out_2[2]));
  Adder adder_4 (
    .a(adder_3_out), .b(left_shift_8_22_out_3), .out(adder_4_out), .cin(adder_3_cout), .cout(adder_4_cout));
  or or_2 (or_2_out, left_shift_8_28_out_2, adder_7_cout);
  left_shift_8 left_shift_8_12 (
    .in_1(left_shift_8_13_out_3), .out_3(left_shift_8_12_out_3), .out_2(left_shift_8_12_out_2[0]));
  left_shift_8 left_shift_8_13 (
    .in_1(left_shift_8_11_out_3), .out_3(left_shift_8_13_out_3), .out_2(left_shift_8_12_out_2[1]));
  Adder adder_5 (
    .a(adder_4_out), .b(left_shift_8_25_out_3), .out(adder_5_out), .cin(adder_4_cout), .cout(adder_5_cout));
  left_shift_8 left_shift_8_14 (
    .in_1(one_on_eight_3_out_3), .out_3(left_shift_8_14_out_3), .out_2(left_shift_8_18_out_2[4]));
  left_shift_8 left_shift_8_15 (
    .in_1(left_shift_8_14_out_3), .out_3(left_shift_8_15_out_3), .out_2(left_shift_8_18_out_2[3]));
  Adder adder_6 (
    .a(adder_5_out), .b(left_shift_8_27_out_3), .out(adder_6_out), .cin(adder_5_cout), .cout(adder_6_cout));
  left_shift_8 left_shift_8_16 (
    .in_1(left_shift_8_15_out_3), .out_3(left_shift_8_16_out_3), .out_2(left_shift_8_18_out_2[2]));
  left_shift_8 left_shift_8_17 (
    .in_1(left_shift_8_16_out_3), .out_3(left_shift_8_17_out_3), .out_2(left_shift_8_18_out_2[1]));
  Adder adder_7 (.a(adder_6_out), .b(left_shift_8_28_out_3), .out(out_4), .cin(adder_6_cout), .cout(adder_7_cout));
  left_shift_8 left_shift_8_18 (
    .in_1(left_shift_8_17_out_3), .out_3(left_shift_8_18_out_3), .out_2(left_shift_8_18_out_2[0]));
  left_shift_8 left_shift_8_19 (
    .in_1(one_on_eight_4_out_3), .out_3(left_shift_8_19_out_3), .out_2(left_shift_8_22_out_2[3]));
  left_shift_8 left_shift_8_20 (
    .in_1(left_shift_8_19_out_3), .out_3(left_shift_8_20_out_3), .out_2(left_shift_8_22_out_2[2]));
  left_shift_8 left_shift_8_21 (
    .in_1(left_shift_8_20_out_3), .out_3(left_shift_8_21_out_3), .out_2(left_shift_8_22_out_2[1]));
  left_shift_8 left_shift_8_22 (
    .in_1(left_shift_8_21_out_3), .out_3(left_shift_8_22_out_3), .out_2(left_shift_8_22_out_2[0]));
  left_shift_8 left_shift_8_23 (
    .in_1(one_on_eight_5_out_3), .out_3(left_shift_8_23_out_3), .out_2(left_shift_8_25_out_2[2]));
  left_shift_8 left_shift_8_24 (
    .in_1(left_shift_8_23_out_3), .out_3(left_shift_8_24_out_3), .out_2(left_shift_8_25_out_2[1]));
  left_shift_8 left_shift_8_25 (
    .in_1(left_shift_8_24_out_3), .out_3(left_shift_8_25_out_3), .out_2(left_shift_8_25_out_2[0]));
  left_shift_8 left_shift_8_26 (
    .in_1(one_on_eight_6_out_3), .out_3(left_shift_8_26_out_3), .out_2(left_shift_8_27_out_2[1]));
  left_shift_8 left_shift_8_27 (
    .in_1(left_shift_8_26_out_3), .out_3(left_shift_8_27_out_3), .out_2(left_shift_8_27_out_2[0]));
  left_shift_8 left_shift_8_28 (
    .in_1(one_on_eight_7_out_3), .out_3(left_shift_8_28_out_3), .out_2(left_shift_8_28_out_2));
endmodule

module one_on_eight (
  input  [7:0] in_1,
  input  in_2,
  output [7:0] out_3
);

  and and_1 (out_3[7], in_1[7], in_2);
  and and_2 (out_3[6], in_1[6], in_2);
  and and_3 (out_3[5], in_1[5], in_2);
  and and_4 (out_3[4], in_1[4], in_2);
  and and_5 (out_3[3], in_1[3], in_2);
  and and_6 (out_3[2], in_1[2], in_2);
  and and_7 (out_3[1], in_1[1], in_2);
  and and_8 (out_3[0], in_1[0], in_2);
endmodule

module Division_8 (
  input  [7:0] in_1,
  input  [7:0] in_2,
  output [7:0] out_3,
  output [7:0] out_4
);

  wire [7:0] division_single_unit_1_out_5, division_single_unit_2_out_5, division_single_unit_3_out_5,
       division_single_unit_4_out_5, division_single_unit_5_out_5, division_single_unit_6_out_5,
       division_single_unit_7_out_5;

  Division_Single_Unit division_single_unit_1 (
    .in_2({8{1'b0}}), .in_3(in_2), .out_4(out_3[7]), .out_5(division_single_unit_1_out_5), .in_1(in_1[7]));
  Division_Single_Unit division_single_unit_2 (
    .in_2(division_single_unit_1_out_5), .in_3(in_2), .out_4(out_3[6]), .out_5(division_single_unit_2_out_5),
    .in_1(in_1[6]));
  Division_Single_Unit division_single_unit_3 (
    .in_2(division_single_unit_2_out_5), .in_3(in_2), .out_4(out_3[5]), .out_5(division_single_unit_3_out_5),
    .in_1(in_1[5]));
  Division_Single_Unit division_single_unit_4 (
    .in_2(division_single_unit_3_out_5), .in_3(in_2), .out_4(out_3[4]), .out_5(division_single_unit_4_out_5),
    .in_1(in_1[4]));
  Division_Single_Unit division_single_unit_5 (
    .in_2(division_single_unit_4_out_5), .in_3(in_2), .out_4(out_3[3]), .out_5(division_single_unit_5_out_5),
    .in_1(in_1[3]));
  Division_Single_Unit division_single_unit_6 (
    .in_2(division_single_unit_5_out_5), .in_3(in_2), .out_4(out_3[2]), .out_5(division_single_unit_6_out_5),
    .in_1(in_1[2]));
  Division_Single_Unit division_single_unit_7 (
    .in_2(division_single_unit_6_out_5), .in_3(in_2), .out_4(out_3[1]), .out_5(division_single_unit_7_out_5),
    .in_1(in_1[1]));
  Division_Single_Unit division_single_unit_8 (
    .in_2(division_single_unit_7_out_5), .in_3(in_2), .out_4(out_3[0]), .out_5(out_4), .in_1(in_1[0]));
endmodule

module Division_Single_Unit (
  input  in_1,
  input  [7:0] in_2,
  input  [7:0] in_3,
  output out_4,
  output [7:0] out_5
);

  wire not_2_out;
  wire [7:0] binary_adder_8_1_out_5, not_1_out, push_bits_1_out_4;

  Push_Bits push_bits_1 (.in_1(in_2), .in_2(in_1), .out_4(push_bits_1_out_4));  // open: out_3
  Binary_Adder_8 binary_adder_8_1 (
    .in_1(push_bits_1_out_4), .in_2(not_1_out), .out_5(binary_adder_8_1_out_5), .out_4(out_4), .in_3(1'b1));
  assign not_1_out = ~in_3;  // NOT_Gate not_1, 8 bits wide
  not not_2 (not_2_out, out_4);
  assign out_5 = not_2_out ? push_bits_1_out_4 : 8'bz;  // Controlled_Buffer controlled_buffer_1
  assign out_5 = out_4 ? binary_adder_8_1_out_5 : 8'bz;  // Controlled_Buffer controlled_buffer_2
endmodule

module Push_Bits (
  input  [7:0] in_1,
  input  in_2,
  output out_3,
  output [7:0] out_4
);


  assign out_3 = in_1[7];
  assign out_4 = {in_1[6:0], in_2};
endmodule
